# Fritzing sketch distance_sensor (saved by Fritzing 0.9.10b)
breadboards: 1

parts:
  Part1 = Adafruit T-Cobbler Plus [part_number="Adafruit #1989 and #2028"]
  ADC1 = MCP3008 [package=dil16]
  J3 = Infrared Proximity Sensor [distance_to_obstacle=50%]

nets:
  +3.3V: Part1.+3.3V, ADC1.VDD
  GND: Part1.GND, ADC1.VREF, J3.GND
  N1: Part1.MOSI, ADC1.Din
  N2: Part1.SCLK, ADC1.CLK
  N3: Part1.GPIO5, ADC1.CS/SHDN
  +5V: Part1.+5V, ADC1.DGND, ADC1.AGND, J3.Vcc
  N4: ADC1.CH0, J3.Vout

custom parts:
  Adafruit T-Cobbler Plus: The Raspberry Pi has landed on the Maker World like a 40-GPIO pinned, quad-USB ported, credit card sized bomb of DIY joy. And while you can use most of our great Model B accessories by hooking up our downgrade cable, its probably a good time to upgrade your set up and accessorize using all of the 40 pins. That's why we now carry the Assembled Adafruit Pi T-Cobbler Plus - Breakout + Cable for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
