# Fritzing sketch distance_sensor (saved by Fritzing 0.9.10b)
breadboards: 2

parts:
  Part1 = Adafruit T-Cobbler Plus [part_number="Adafruit #1989 and #2028"]
  ADC1 = MCP3008 [package=dil16]
  J3 = Infrared Proximity Sensor [distance_to_obstacle=50%]
  OLED1 = OLED 128x64 I2C Monochrome Display GND-VDD
  Part4 = 9-DOF IMU L3GD20H + LSM303 [part_number=1714]

nets:
  VDD: Part1.+3.3V, ADC1.VREF, ADC1.VDD, OLED1.VDD, Part4.3.3V
  N1: Part1.SDA, OLED1.SDA, Part4.SDA
  N2: Part1.SCL, OLED1.SCK, Part4.SCL
  GND: Part1.GND, J3.GND, OLED1.GND, Part4.GND
  N3: Part1.MOSI, ADC1.Din
  N4: Part1.SCLK, ADC1.CLK
  N5: Part1.GPIO5, ADC1.CS/SHDN
  +5V: Part1.+5V, ADC1.DGND, ADC1.AGND, J3.Vcc
  N6: ADC1.CH0, J3.Vout

custom parts:
  Adafruit T-Cobbler Plus: The Raspberry Pi has landed on the Maker World like a 40-GPIO pinned, quad-USB ported, credit card sized bomb of DIY joy. And while you can use most of our great Model B accessories by hooking up our downgrade cable, its probably a good time to upgrade your set up and accessorize using all of the 40 pins. That's why we now carry the Assembled Adafruit Pi T-Cobbler Plus - Breakout + Cable for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
  OLED 128x64 I2C Monochrome Display GND-VDD: OLED 128x64 I2C Monochrome Display. Note: there are two variants of this part, this one is the GND VDD SCK SDA variant. The other is VDD GND SCK SDA. Make sure you select the part that matches your module as using the incorrect part will probably destroy your module! In addition the mounting holes are marked on silkscreen but not by default drilled. If you want drilled mounting holes, copy a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
  9-DOF IMU L3GD20H + LSM303: This inertial-measurement-unit combines 2 of the best quality sensors available on the market to give you 9 axes of data: 3 axes of accelerometer data, 3 axes gyroscopic, and 3 axes magnetic (compass). We tested many different 'combination' sensors and found these were the best value, with stable and reliable readings.
